// Logisim project Contador Binario.circ as structural Verilog: 12 circuits, main circuit main
module Contador_4_Bits_com_display (
  input  _0___Crescente__1___Decrescente,
  input  in_2,
  input  in_3,
  input  in_4,
  input  in_5
);

  wire and_1_out, and_2_out, and_3_out, and_4_out, and_5_out, and_6_out, and_7_out, and_8_out, and_9_out,
       and_10_out, clock_1_out, conversor_d_1_1_a_2, conversor_d_1_1_b_2, conversor_d_1_1_c_2,
       conversor_d_1_1_d_2, conversor_d_1_1_e, conversor_d_1_1_f, conversor_d_1_1_g, conversor_d_15_1_a_2,
       conversor_d_15_1_b_2, conversor_d_15_1_c_2, conversor_d_15_1_d_2, conversor_d_15_1_e,
       conversor_d_15_1_f, conversor_d_15_1_g, flip_flop_t_2_0_1_q, flip_flop_t_2_0_1_q_prime,
       flip_flop_t_2_0_2_q, flip_flop_t_2_0_2_q_prime, flip_flop_t_2_0_3_q, flip_flop_t_2_0_3_q_prime,
       flip_flop_t_2_0_4_q, flip_flop_t_2_0_4_q_prime, not_1_out, not_2_out, not_3_out, not_4_out, not_5_out,
       or_1_out, or_2_out, or_3_out, or_4_out;

  Clock clock_1 (.out(clock_1_out));
  not not_1 (not_1_out, _0___Crescente__1___Decrescente);
  and and_1 (and_1_out, clock_1_out, _0___Crescente__1___Decrescente);
  and and_2 (and_2_out, clock_1_out, not_1_out);
  Flip_Flop_T_2_0 flip_flop_t_2_0_1 (
    .Clock(and_2_out), .T(1'b1), .Reset(in_2), .Q(flip_flop_t_2_0_1_q), .Q_prime(flip_flop_t_2_0_1_q_prime));
  not not_2 (not_2_out, and_1_out);
  and and_3 (and_3_out, flip_flop_t_2_0_1_q, not_2_out);
  Conversor_D_1 conversor_d_1_1 (
    .A(or_4_out), .B(or_3_out), .C(or_2_out), .D(or_1_out), .a_2(conversor_d_1_1_a_2),
    .b_2(conversor_d_1_1_b_2), .c_2(conversor_d_1_1_c_2), .d_2(conversor_d_1_1_d_2), .e(conversor_d_1_1_e),
    .f(conversor_d_1_1_f), .g(conversor_d_1_1_g));
  and and_4 (and_4_out, flip_flop_t_2_0_1_q_prime, and_1_out);
  or or_1 (or_1_out, and_3_out, and_4_out);
  _7_Segment_Display u_7_segment_display_1 (
    .g(conversor_d_1_1_g), .f(conversor_d_1_1_f), .a(conversor_d_1_1_a_2), .b(conversor_d_1_1_b_2),
    .e(conversor_d_1_1_e), .d(conversor_d_1_1_d_2), .c(conversor_d_1_1_c_2));  // open: dp
  Flip_Flop_T_2_0 flip_flop_t_2_0_2 (
    .Clock(or_1_out), .T(1'b1), .Reset(in_3), .Q(flip_flop_t_2_0_2_q), .Q_prime(flip_flop_t_2_0_2_q_prime));
  not not_3 (not_3_out, and_1_out);
  and and_5 (and_5_out, flip_flop_t_2_0_2_q, not_3_out);
  _7_Segment_Display u_7_segment_display_2 (
    .g(conversor_d_15_1_g), .f(conversor_d_15_1_f), .a(conversor_d_15_1_a_2), .b(conversor_d_15_1_b_2),
    .e(conversor_d_15_1_e), .d(conversor_d_15_1_d_2), .c(conversor_d_15_1_c_2));  // open: dp
  Conversor_D_15 conversor_d_15_1 (
    .A(or_4_out), .B(or_3_out), .C(or_2_out), .D(or_1_out), .a_2(conversor_d_15_1_a_2),
    .b_2(conversor_d_15_1_b_2), .c_2(conversor_d_15_1_c_2), .d_2(conversor_d_15_1_d_2),
    .e(conversor_d_15_1_e), .f(conversor_d_15_1_f), .g(conversor_d_15_1_g));
  and and_6 (and_6_out, flip_flop_t_2_0_2_q_prime, and_1_out);
  or or_2 (or_2_out, and_5_out, and_6_out);
  Flip_Flop_T_2_0 flip_flop_t_2_0_3 (
    .Clock(or_2_out), .T(1'b1), .Reset(in_4), .Q(flip_flop_t_2_0_3_q), .Q_prime(flip_flop_t_2_0_3_q_prime));
  not not_4 (not_4_out, and_1_out);
  and and_7 (and_7_out, flip_flop_t_2_0_3_q_prime, and_1_out);
  and and_8 (and_8_out, flip_flop_t_2_0_3_q, not_4_out);
  or or_3 (or_3_out, and_8_out, and_7_out);
  Flip_Flop_T_2_0 flip_flop_t_2_0_4 (
    .Clock(or_3_out), .T(1'b1), .Reset(in_5), .Q(flip_flop_t_2_0_4_q), .Q_prime(flip_flop_t_2_0_4_q_prime));
  not not_5 (not_5_out, and_1_out);
  and and_9 (and_9_out, flip_flop_t_2_0_4_q, not_5_out);
  or or_4 (or_4_out, and_9_out, and_10_out);
  and and_10 (and_10_out, flip_flop_t_2_0_4_q_prime, and_1_out);
endmodule

module main (
  input  A,
  input  A_2,
  input  A_3,
  input  A_4,
  input  B,
  input  B_2,
  input  B_3,
  input  B_4,
  input  C,
  input  C_2,
  input  C_3,
  input  C_4,
  output out_13,
  output out_14,
  output out_15,
  output out_16
);

  wire clock_1_out, conversor_d_9_1_a_2, conversor_d_9_1_b_2, conversor_d_9_1_c_2, conversor_d_9_1_d_2,
       conversor_d_9_1_e, conversor_d_9_1_f, conversor_d_9_1_g, conversor_d_9_2_a_2, conversor_d_9_2_b_2,
       conversor_d_9_2_c_2, conversor_d_9_2_d_2, conversor_d_9_2_e, conversor_d_9_2_f, conversor_d_9_2_g,
       conversor_d_9_3_a_2, conversor_d_9_3_b_2, conversor_d_9_3_c_2, conversor_d_9_3_d_2, conversor_d_9_3_e,
       conversor_d_9_3_f, conversor_d_9_3_g, conversor_d_9_4_a_2, conversor_d_9_4_b_2, conversor_d_9_4_c_2,
       conversor_d_9_4_d_2, conversor_d_9_4_e, conversor_d_9_4_f, conversor_d_9_4_g;

  Conversor_D_9 conversor_d_9_1 (
    .A(A), .B(B), .C(C), .D(out_16), .a_2(conversor_d_9_1_a_2), .b_2(conversor_d_9_1_b_2),
    .c_2(conversor_d_9_1_c_2), .d_2(conversor_d_9_1_d_2), .e(conversor_d_9_1_e), .f(conversor_d_9_1_f),
    .g(conversor_d_9_1_g));
  Clock clock_1 (.out(clock_1_out));
  T_Flip_Flop #(.trigger("falling")) t_ff_1 (.clk(clock_1_out), .T(1'b1), .Q(out_13));  // open: Qn, preset, reset, en
  _7_Segment_Display u_7_segment_display_1 (
    .g(conversor_d_9_1_g), .f(conversor_d_9_1_f), .a(conversor_d_9_1_a_2), .b(conversor_d_9_1_b_2),
    .e(conversor_d_9_1_e), .d(conversor_d_9_1_d_2), .c(conversor_d_9_1_c_2));  // open: dp
  Conversor_D_9 conversor_d_9_2 (
    .A(A_2), .B(B_2), .C(C_2), .D(out_15), .a_2(conversor_d_9_2_a_2), .b_2(conversor_d_9_2_b_2),
    .c_2(conversor_d_9_2_c_2), .d_2(conversor_d_9_2_d_2), .e(conversor_d_9_2_e), .f(conversor_d_9_2_f),
    .g(conversor_d_9_2_g));
  T_Flip_Flop #(.trigger("falling")) t_ff_2 (.clk(out_13), .T(1'b1), .Q(out_14));  // open: Qn, preset, reset, en
  T_Flip_Flop #(.trigger("falling")) t_ff_3 (.clk(out_14), .T(1'b1), .Q(out_15));  // open: Qn, preset, reset, en
  _7_Segment_Display u_7_segment_display_2 (
    .g(conversor_d_9_2_g), .f(conversor_d_9_2_f), .a(conversor_d_9_2_a_2), .b(conversor_d_9_2_b_2),
    .e(conversor_d_9_2_e), .d(conversor_d_9_2_d_2), .c(conversor_d_9_2_c_2));  // open: dp
  T_Flip_Flop #(.trigger("falling")) t_ff_4 (.clk(out_15), .T(1'b1), .Q(out_16));  // open: Qn, preset, reset, en
  Conversor_D_9 conversor_d_9_3 (
    .A(A_3), .B(B_3), .C(C_3), .D(out_14), .a_2(conversor_d_9_3_a_2), .b_2(conversor_d_9_3_b_2),
    .c_2(conversor_d_9_3_c_2), .d_2(conversor_d_9_3_d_2), .e(conversor_d_9_3_e), .f(conversor_d_9_3_f),
    .g(conversor_d_9_3_g));
  _7_Segment_Display u_7_segment_display_3 (
    .g(conversor_d_9_3_g), .f(conversor_d_9_3_f), .a(conversor_d_9_3_a_2), .b(conversor_d_9_3_b_2),
    .e(conversor_d_9_3_e), .d(conversor_d_9_3_d_2), .c(conversor_d_9_3_c_2));  // open: dp
  Conversor_D_9 conversor_d_9_4 (
    .A(A_4), .B(B_4), .C(C_4), .D(out_13), .a_2(conversor_d_9_4_a_2), .b_2(conversor_d_9_4_b_2),
    .c_2(conversor_d_9_4_c_2), .d_2(conversor_d_9_4_d_2), .e(conversor_d_9_4_e), .f(conversor_d_9_4_f),
    .g(conversor_d_9_4_g));
  _7_Segment_Display u_7_segment_display_4 (
    .g(conversor_d_9_4_g), .f(conversor_d_9_4_f), .a(conversor_d_9_4_a_2), .b(conversor_d_9_4_b_2),
    .e(conversor_d_9_4_e), .d(conversor_d_9_4_d_2), .c(conversor_d_9_4_c_2));  // open: dp
endmodule

module Up_Down (
  input  Decrescente,
  input  A,
  input  A_2,
  input  A_3,
  input  A_4,
  input  B,
  input  B_2,
  input  B_3,
  input  B_4,
  input  C,
  input  C_2,
  input  C_3,
  input  C_4,
  output out_14,
  output out_15,
  output out_16,
  output out_17
);

  wire and_1_out, and_2_out, and_3_out, and_4_out, and_5_out, and_6_out, and_7_out, and_8_out, Clock_out,
       conversor_d_9_1_a_2, conversor_d_9_1_b_2, conversor_d_9_1_c_2, conversor_d_9_1_d_2, conversor_d_9_1_e,
       conversor_d_9_1_f, conversor_d_9_1_g, conversor_d_9_2_a_2, conversor_d_9_2_b_2, conversor_d_9_2_c_2,
       conversor_d_9_2_d_2, conversor_d_9_2_e, conversor_d_9_2_f, conversor_d_9_2_g, conversor_d_9_3_a_2,
       conversor_d_9_3_b_2, conversor_d_9_3_c_2, conversor_d_9_3_d_2, conversor_d_9_3_e, conversor_d_9_3_f,
       conversor_d_9_3_g, conversor_d_9_4_a_2, conversor_d_9_4_b_2, conversor_d_9_4_c_2, conversor_d_9_4_d_2,
       conversor_d_9_4_e, conversor_d_9_4_f, conversor_d_9_4_g, not_1_out, not_2_out, not_3_out, not_4_out,
       t_ff_1_q, t_ff_1_qn, t_ff_2_q, t_ff_2_qn, t_ff_3_q, t_ff_3_qn, t_ff_4_q, t_ff_4_qn;

  Clock Clock (.out(Clock_out));
  Conversor_D_9 conversor_d_9_1 (
    .A(A), .B(B), .C(C), .D(out_17), .a_2(conversor_d_9_1_a_2), .b_2(conversor_d_9_1_b_2),
    .c_2(conversor_d_9_1_c_2), .d_2(conversor_d_9_1_d_2), .e(conversor_d_9_1_e), .f(conversor_d_9_1_f),
    .g(conversor_d_9_1_g));
  T_Flip_Flop #(.trigger("falling")) t_ff_1 (
    .clk(Clock_out), .T(1'b1), .Q(t_ff_1_q), .Qn(t_ff_1_qn));  // open: preset, reset, en
  and and_1 (and_1_out, t_ff_1_q, not_1_out);
  _7_Segment_Display u_7_segment_display_1 (
    .g(conversor_d_9_1_g), .f(conversor_d_9_1_f), .a(conversor_d_9_1_a_2), .b(conversor_d_9_1_b_2),
    .e(conversor_d_9_1_e), .d(conversor_d_9_1_d_2), .c(conversor_d_9_1_c_2));  // open: dp
  not not_1 (not_1_out, Decrescente);
  and and_2 (and_2_out, t_ff_1_qn, Decrescente);
  or or_1 (out_14, and_1_out, and_2_out);
  T_Flip_Flop #(.trigger("falling")) t_ff_2 (
    .clk(out_14), .T(1'b1), .Q(t_ff_2_q), .Qn(t_ff_2_qn));  // open: preset, reset, en
  and and_3 (and_3_out, t_ff_2_q, not_2_out);
  Conversor_D_9 conversor_d_9_2 (
    .A(A_2), .B(B_2), .C(C_2), .D(out_16), .a_2(conversor_d_9_2_a_2), .b_2(conversor_d_9_2_b_2),
    .c_2(conversor_d_9_2_c_2), .d_2(conversor_d_9_2_d_2), .e(conversor_d_9_2_e), .f(conversor_d_9_2_f),
    .g(conversor_d_9_2_g));
  not not_2 (not_2_out, Decrescente);
  and and_4 (and_4_out, t_ff_2_qn, Decrescente);
  or or_2 (out_15, and_3_out, and_4_out);
  _7_Segment_Display u_7_segment_display_2 (
    .g(conversor_d_9_2_g), .f(conversor_d_9_2_f), .a(conversor_d_9_2_a_2), .b(conversor_d_9_2_b_2),
    .e(conversor_d_9_2_e), .d(conversor_d_9_2_d_2), .c(conversor_d_9_2_c_2));  // open: dp
  T_Flip_Flop #(.trigger("falling")) t_ff_3 (
    .clk(out_15), .T(1'b1), .Q(t_ff_3_q), .Qn(t_ff_3_qn));  // open: preset, reset, en
  not not_3 (not_3_out, Decrescente);
  and and_5 (and_5_out, t_ff_3_q, not_3_out);
  or or_3 (out_16, and_5_out, and_6_out);
  Conversor_D_9 conversor_d_9_3 (
    .A(A_3), .B(B_3), .C(C_3), .D(out_15), .a_2(conversor_d_9_3_a_2), .b_2(conversor_d_9_3_b_2),
    .c_2(conversor_d_9_3_c_2), .d_2(conversor_d_9_3_d_2), .e(conversor_d_9_3_e), .f(conversor_d_9_3_f),
    .g(conversor_d_9_3_g));
  and and_6 (and_6_out, t_ff_3_qn, Decrescente);
  _7_Segment_Display u_7_segment_display_3 (
    .g(conversor_d_9_3_g), .f(conversor_d_9_3_f), .a(conversor_d_9_3_a_2), .b(conversor_d_9_3_b_2),
    .e(conversor_d_9_3_e), .d(conversor_d_9_3_d_2), .c(conversor_d_9_3_c_2));  // open: dp
  T_Flip_Flop #(.trigger("falling")) t_ff_4 (
    .clk(out_16), .T(1'b1), .Q(t_ff_4_q), .Qn(t_ff_4_qn));  // open: preset, reset, en
  not not_4 (not_4_out, Decrescente);
  and and_7 (and_7_out, t_ff_4_q, not_4_out);
  and and_8 (and_8_out, t_ff_4_qn, Decrescente);
  or or_4 (out_17, and_7_out, and_8_out);
  Conversor_D_9 conversor_d_9_4 (
    .A(A_4), .B(B_4), .C(C_4), .D(out_14), .a_2(conversor_d_9_4_a_2), .b_2(conversor_d_9_4_b_2),
    .c_2(conversor_d_9_4_c_2), .d_2(conversor_d_9_4_d_2), .e(conversor_d_9_4_e), .f(conversor_d_9_4_f),
    .g(conversor_d_9_4_g));
  _7_Segment_Display u_7_segment_display_4 (
    .g(conversor_d_9_4_g), .f(conversor_d_9_4_f), .a(conversor_d_9_4_a_2), .b(conversor_d_9_4_b_2),
    .e(conversor_d_9_4_e), .d(conversor_d_9_4_d_2), .c(conversor_d_9_4_c_2));  // open: dp
endmodule

module Conversor_D_9 (
  input  A,
  input  B,
  input  C,
  input  D,
  output a_2,
  output b_2,
  output c_2,
  output d_2,
  output e,
  output f,
  output g
);

  wire and_1_out, and_2_out, and_3_out, and_4_out, and_5_out, and_6_out, and_7_out, and_8_out, and_9_out,
       and_10_out, and_11_out, and_12_out, and_13_out, and_14_out, and_15_out, and_16_out, not_1_out,
       not_2_out, not_3_out, not_4_out, not_5_out, not_6_out, not_7_out, not_8_out, not_9_out, not_10_out,
       not_11_out, not_12_out, not_13_out, not_14_out, not_15_out, not_16_out, not_17_out, not_18_out,
       not_19_out, not_20_out, not_21_out;

  not not_1 (not_1_out, B);
  and and_1 (and_1_out, not_1_out, not_2_out);
  not not_2 (not_2_out, D);
  and and_2 (and_2_out, B, D);
  not not_3 (not_3_out, B);
  not not_4 (not_4_out, C);
  and and_3 (and_3_out, not_4_out, not_5_out);
  not not_5 (not_5_out, D);
  and and_4 (and_4_out, C, D);
  not not_6 (not_6_out, C);
  or or_1 (c_2, not_6_out, D, B);
  not not_7 (not_7_out, B);
  and and_5 (and_5_out, not_7_out, not_8_out);
  not not_8 (not_8_out, D);
  not not_9 (not_9_out, B);
  and and_6 (and_6_out, not_9_out, C);
  and and_7 (and_7_out, C, not_10_out);
  not not_10 (not_10_out, D);
  not not_11 (not_11_out, C);
  and and_8 (and_8_out, B, not_11_out, D);
  not not_12 (not_12_out, B);
  and and_9 (and_9_out, not_12_out, not_13_out);
  not not_13 (not_13_out, D);
  and and_10 (and_10_out, C, not_14_out);
  not not_14 (not_14_out, D);
  not not_15 (not_15_out, C);
  and and_11 (and_11_out, not_15_out, not_16_out);
  not not_16 (not_16_out, D);
  and and_12 (and_12_out, B, not_17_out);
  not not_17 (not_17_out, C);
  and and_13 (and_13_out, B, not_18_out);
  not not_18 (not_18_out, D);
  not not_19 (not_19_out, B);
  and and_14 (and_14_out, not_19_out, C);
  and and_15 (and_15_out, B, not_20_out);
  not not_20 (not_20_out, C);
  and and_16 (and_16_out, B, not_21_out);
  not not_21 (not_21_out, D);
  or or_2 (a_2, and_1_out, C, and_2_out, A);
  or or_3 (b_2, not_3_out, and_3_out, and_4_out);
  or or_4 (d_2, and_5_out, and_6_out, and_7_out, and_8_out, A);
  or or_5 (e, and_9_out, and_10_out);
  or or_6 (f, and_11_out, and_12_out, and_13_out, A);
  or or_7 (g, and_14_out, and_15_out, and_16_out, A);
endmodule

module Conversor_D_1 (
  input  A,
  input  B,
  input  C,
  input  D,
  output a_2,
  output b_2,
  output c_2,
  output d_2,
  output e,
  output f,
  output g
);

  wire and_1_out, and_2_out, and_3_out, and_4_out, not_1_out, not_2_out, not_3_out, not_4_out, not_5_out,
       not_6_out, not_7_out, not_8_out, not_9_out, not_10_out, not_11_out, not_12_out;

  not not_1 (not_1_out, A);
  not not_2 (not_2_out, B);
  and and_1 (and_1_out, not_2_out, not_3_out);
  not not_3 (not_3_out, C);
  not not_4 (not_4_out, A);
  not not_5 (not_5_out, B);
  and and_2 (and_2_out, not_5_out, not_6_out);
  not not_6 (not_6_out, C);
  not not_7 (not_7_out, A);
  not not_8 (not_8_out, B);
  and and_3 (and_3_out, not_8_out, not_9_out);
  not not_9 (not_9_out, C);
  not not_10 (not_10_out, A);
  not not_11 (not_11_out, B);
  and and_4 (and_4_out, not_11_out, not_12_out);
  not not_12 (not_12_out, C);
  or or_1 (a_2, not_1_out, and_1_out);
  or or_2 (d_2, not_4_out, and_2_out);
  or or_3 (e, not_7_out, and_3_out);
  or or_4 (f, not_10_out, and_4_out);

  assign b_2 = 1'b1;
  assign c_2 = 1'b1;
  assign g = 1'b0;
endmodule

module Conversor_D_15 (
  input  A,
  input  B,
  input  C,
  input  D,
  output a_2,
  output b_2,
  output c_2,
  output d_2,
  output e,
  output f,
  output g
);

  wire and_1_out, and_2_out, and_3_out, and_4_out, and_5_out, and_6_out, and_7_out, and_8_out, and_9_out,
       and_10_out, and_11_out, and_12_out, and_13_out, and_14_out, and_15_out, and_16_out, and_17_out,
       and_18_out, and_19_out, and_20_out, and_21_out, and_22_out, and_23_out, and_24_out, and_25_out,
       and_26_out, and_27_out, and_28_out, and_29_out, and_30_out, and_31_out, not_1_out, not_2_out,
       not_3_out, not_4_out, not_5_out, not_6_out, not_7_out, not_8_out, not_9_out, not_10_out, not_11_out,
       not_12_out, not_13_out, not_14_out, not_15_out, not_16_out, not_17_out, not_18_out, not_19_out,
       not_20_out, not_21_out, not_22_out, not_23_out, not_24_out, not_25_out, not_26_out, not_27_out,
       not_28_out, not_29_out, not_30_out, not_31_out, not_32_out, not_33_out, not_34_out, not_35_out,
       not_36_out, not_37_out, not_38_out, not_39_out, not_40_out, not_41_out, not_42_out, not_43_out;

  not not_1 (not_1_out, B);
  and and_1 (and_1_out, not_1_out, not_2_out);
  not not_2 (not_2_out, D);
  not not_3 (not_3_out, A);
  and and_2 (and_2_out, not_3_out, C);
  and and_3 (and_3_out, B, D);
  and and_4 (and_4_out, A, not_4_out);
  not not_4 (not_4_out, C);
  not not_5 (not_5_out, B);
  not not_6 (not_6_out, C);
  and and_5 (and_5_out, not_6_out, not_7_out);
  not not_7 (not_7_out, D);
  not not_8 (not_8_out, A);
  and and_6 (and_6_out, not_8_out, C, D);
  and and_7 (and_7_out, A, not_9_out);
  not not_9 (not_9_out, C);
  and and_8 (and_8_out, A, not_10_out);
  not not_10 (not_10_out, D);
  not not_11 (not_11_out, A);
  and and_9 (and_9_out, not_11_out, not_12_out);
  not not_12 (not_12_out, C);
  and and_10 (and_10_out, B, C);
  and and_11 (and_11_out, A, not_13_out);
  not not_13 (not_13_out, B);
  not not_14 (not_14_out, B);
  and and_12 (and_12_out, not_14_out, not_15_out);
  not not_15 (not_15_out, D);
  not not_16 (not_16_out, A);
  not not_17 (not_17_out, B);
  and and_13 (and_13_out, not_16_out, not_17_out, C);
  not not_18 (not_18_out, A);
  and and_14 (and_14_out, not_18_out, C, not_19_out);
  not not_19 (not_19_out, D);
  not not_20 (not_20_out, C);
  and and_15 (and_15_out, B, not_20_out, D);
  and and_16 (and_16_out, A, not_21_out);
  not not_21 (not_21_out, C);
  and and_17 (and_17_out, A, B, D);
  not not_22 (not_22_out, B);
  and and_18 (and_18_out, not_22_out, not_23_out);
  not not_23 (not_23_out, D);
  not not_24 (not_24_out, A);
  and and_19 (and_19_out, not_24_out, C, not_25_out);
  not not_25 (not_25_out, D);
  and and_20 (and_20_out, A, not_26_out, not_27_out);
  not not_26 (not_26_out, C);
  not not_27 (not_27_out, D);
  not not_28 (not_28_out, A);
  not not_29 (not_29_out, C);
  and and_21 (and_21_out, not_28_out, not_29_out, not_30_out);
  not not_30 (not_30_out, D);
  not not_31 (not_31_out, A);
  and and_22 (and_22_out, not_31_out, B, not_32_out);
  not not_32 (not_32_out, C);
  not not_33 (not_33_out, A);
  and and_23 (and_23_out, not_33_out, B, not_34_out);
  not not_34 (not_34_out, D);
  and and_24 (and_24_out, A, not_35_out, not_36_out);
  not not_35 (not_35_out, B);
  not not_36 (not_36_out, C);
  not not_37 (not_37_out, B);
  and and_25 (and_25_out, A, not_37_out, not_38_out);
  not not_38 (not_38_out, D);
  and and_26 (and_26_out, A, B, C);
  not not_39 (not_39_out, A);
  and and_27 (and_27_out, not_39_out, not_40_out, C);
  not not_40 (not_40_out, B);
  and and_28 (and_28_out, B, not_41_out);
  not not_41 (not_41_out, C);
  and and_29 (and_29_out, B, not_42_out);
  not not_42 (not_42_out, D);
  and and_30 (and_30_out, A, not_43_out);
  not not_43 (not_43_out, C);
  and and_31 (and_31_out, A, B);
  or or_1 (a_2, and_1_out, and_2_out, and_3_out, and_4_out);
  or or_2 (b_2, not_5_out, and_5_out, and_6_out, and_7_out, and_8_out);
  or or_3 (c_2, and_9_out, D, and_10_out, and_11_out);
  or or_4 (e, and_18_out, and_19_out, and_20_out);
  or or_5 (g, and_27_out, and_28_out, and_29_out, and_30_out, and_31_out);
  or or_6 (d_2, and_12_out, and_13_out, and_14_out, and_15_out, and_16_out, and_17_out);
  or or_7 (f, and_21_out, and_22_out, and_23_out, and_24_out, and_25_out, and_26_out);
endmodule

module Flip_Flop_T (
  input  T,
  input  CLK,
  input  in_3,
  output Q,
  output Q_prime
);

  wire and_1_out, and_2_out;

  and and_1 (and_1_out, Q, T, CLK);
  and and_2 (and_2_out, CLK, T, Q_prime);
  nor nor_1 (Q, and_1_out, in_3, Q_prime);
  nor nor_2 (Q_prime, and_2_out, in_3, Q);

  // Notes on the sheet:
  //   Oscilacao aparente
endmodule

module Flip_Flop_T_2_0 (
  input  Clock,
  input  T,
  input  Reset,
  output Q,
  output Q_prime
);

  wire nand_1_out, nand_2_out, nand_3_out, nand_4_out, nand_5_out, nand_6_out, not_1_out, not_2_out;

  not not_1 (not_1_out, Clock);
  nand nand_1 (nand_1_out, Q_prime, T, Clock);
  nand nand_2 (nand_2_out, Clock, T, Q);
  not not_2 (not_2_out, Reset);
  nand nand_3 (nand_3_out, nand_1_out, nand_4_out);
  nand nand_4 (nand_4_out, nand_3_out, nand_2_out, not_2_out);
  nand nand_5 (nand_5_out, nand_3_out, not_1_out);
  nand nand_6 (nand_6_out, nand_4_out, not_1_out);
  nand nand_7 (Q, not_2_out, nand_5_out, Q_prime);
  nand nand_8 (Q_prime, Q, nand_6_out, not_2_out);

  // Notes on the sheet:
  //   Master Slave
endmodule

module teste (
  input  in_1,
  input  in_2,
  input  in_3,
  input  in_4,
  input  in_5,
  input  in_6,
  input  in_7,
  input  in_8,
  output out_9,
  output out_10,
  output out_11,
  output out_12,
  output out_13,
  output out_14,
  output out_15,
  output out_16,
  output out_17,
  output out_18
);

  wire and_1_out, clock_1_out, clock_2_out, clock_3_out, conversor_d_1_1_a_2, conversor_d_1_1_b_2,
       conversor_d_1_1_c_2, conversor_d_1_1_d_2, conversor_d_1_1_e, conversor_d_1_1_f, conversor_d_1_1_g,
       conversor_d_9_1_a_2, conversor_d_9_1_b_2, conversor_d_9_1_c_2, conversor_d_9_1_d_2, conversor_d_9_1_e,
       conversor_d_9_1_f, conversor_d_9_1_g, conversor_d_9_2_a_2, conversor_d_9_2_b_2, conversor_d_9_2_c_2,
       conversor_d_9_2_d_2, conversor_d_9_2_e, conversor_d_9_2_f, conversor_d_9_2_g, conversor_d_15_1_a_2,
       conversor_d_15_1_b_2, conversor_d_15_1_c_2, conversor_d_15_1_d_2, conversor_d_15_1_e,
       conversor_d_15_1_f, conversor_d_15_1_g, or_1_out, undriven;

  Conversor_D_1 conversor_d_1_1 (
    .A(out_14), .B(out_13), .C(out_12), .D(out_11), .a_2(conversor_d_1_1_a_2), .b_2(conversor_d_1_1_b_2),
    .c_2(conversor_d_1_1_c_2), .d_2(conversor_d_1_1_d_2), .e(conversor_d_1_1_e), .f(conversor_d_1_1_f),
    .g(conversor_d_1_1_g));
  Conversor_D_15 conversor_d_15_1 (
    .A(out_14), .B(out_13), .C(out_12), .D(out_11), .a_2(conversor_d_15_1_a_2), .b_2(conversor_d_15_1_b_2),
    .c_2(conversor_d_15_1_c_2), .d_2(conversor_d_15_1_d_2), .e(conversor_d_15_1_e), .f(conversor_d_15_1_f),
    .g(conversor_d_15_1_g));
  _7_Segment_Display u_7_segment_display_1 (
    .g(conversor_d_1_1_g), .f(conversor_d_1_1_f), .a(conversor_d_1_1_a_2), .b(conversor_d_1_1_b_2),
    .e(conversor_d_1_1_e), .d(conversor_d_1_1_d_2), .c(conversor_d_1_1_c_2));  // open: dp
  _7_Segment_Display u_7_segment_display_2 (
    .g(conversor_d_15_1_g), .f(conversor_d_15_1_f), .a(conversor_d_15_1_a_2), .b(conversor_d_15_1_b_2),
    .e(conversor_d_15_1_e), .d(conversor_d_15_1_d_2), .c(conversor_d_15_1_c_2));  // open: dp
  Clock clock_1 (.out(clock_1_out));
  Flip_Flop_T_2_0 flip_flop_t_2_0_1 (.Clock(clock_1_out), .T(1'b1), .Reset(in_2), .Q(out_11));  // open: Q_prime
  Flip_Flop_T_2_0 flip_flop_t_2_0_2 (.Clock(out_11), .T(1'b1), .Reset(in_3), .Q(out_12));  // open: Q_prime
  J_K_Flip_Flop #(.trigger("falling")) j_k_ff_1 (
    .J(in_1), .clk(clock_2_out), .K(in_1), .Q(out_9), .Qn(out_10));  // open: preset, en, reset
  Clock clock_2 (.out(clock_2_out));
  Flip_Flop_T_2_0 flip_flop_t_2_0_3 (.Clock(out_12), .T(1'b1), .Reset(in_4), .Q(out_13));  // open: Q_prime
  Flip_Flop_T_2_0 flip_flop_t_2_0_4 (.Clock(out_13), .T(1'b1), .Reset(in_5), .Q(out_14));  // open: Q_prime
  Conversor_D_9 conversor_d_9_1 (
    .A(in_6), .B(in_7), .C(in_8), .D(and_1_out), .a_2(conversor_d_9_1_a_2), .b_2(conversor_d_9_1_b_2),
    .c_2(conversor_d_9_1_c_2), .d_2(conversor_d_9_1_d_2), .e(conversor_d_9_1_e), .f(conversor_d_9_1_f),
    .g(conversor_d_9_1_g));
  Conversor_D_9 conversor_d_9_2 (
    .A(out_18), .B(out_17), .C(out_16), .D(out_15), .a_2(conversor_d_9_2_a_2), .b_2(conversor_d_9_2_b_2),
    .c_2(conversor_d_9_2_c_2), .d_2(conversor_d_9_2_d_2), .e(conversor_d_9_2_e), .f(conversor_d_9_2_f),
    .g(conversor_d_9_2_g));
  _7_Segment_Display u_7_segment_display_3 (
    .g(conversor_d_9_1_g), .f(conversor_d_9_1_f), .a(conversor_d_9_1_a_2), .b(conversor_d_9_1_b_2),
    .e(conversor_d_9_1_e), .d(conversor_d_9_1_d_2), .c(conversor_d_9_1_c_2));  // open: dp
  _7_Segment_Display u_7_segment_display_4 (
    .g(conversor_d_9_2_g), .f(conversor_d_9_2_f), .a(conversor_d_9_2_a_2), .b(conversor_d_9_2_b_2),
    .e(conversor_d_9_2_e), .d(conversor_d_9_2_d_2), .c(conversor_d_9_2_c_2));  // open: dp
  Clock clock_3 (.out(clock_3_out));
  T_Flip_Flop #(.trigger("falling")) t_ff_1 (
    .clk(clock_3_out), .T(1'b1), .Q(out_15), .reset(undriven));  // open: Qn, preset, en
  T_Flip_Flop #(.trigger("falling")) t_ff_2 (
    .clk(out_15), .T(1'b1), .Q(out_16), .reset(undriven));  // open: Qn, preset, en
  T_Flip_Flop #(.trigger("falling")) t_ff_3 (
    .clk(out_16), .T(1'b1), .Q(out_17), .reset(undriven));  // open: Qn, preset, en
  or or_1 (or_1_out, out_16, out_17);
  and and_1 (and_1_out, or_1_out, out_18);
  T_Flip_Flop #(.trigger("falling")) t_ff_4 (
    .clk(out_17), .T(1'b1), .Q(out_18), .reset(undriven));  // open: Qn, preset, en
endmodule

module teste_2 (
  input  Decrescente,
  input  in_2,
  input  in_3,
  input  in_4,
  input  in_5
);

  wire and_1_out, and_2_out, and_3_out, and_4_out, and_5_out, and_6_out, and_7_out, and_8_out, and_9_out,
       and_10_out, and_11_out, clock_1_out, conversor_d_1_1_a_2, conversor_d_1_1_b_2, conversor_d_1_1_c_2,
       conversor_d_1_1_d_2, conversor_d_1_1_e, conversor_d_1_1_f, conversor_d_1_1_g, conversor_d_15_1_a_2,
       conversor_d_15_1_b_2, conversor_d_15_1_c_2, conversor_d_15_1_d_2, conversor_d_15_1_e,
       conversor_d_15_1_f, conversor_d_15_1_g, not_1_out, not_2_out, not_3_out, not_4_out, not_5_out,
       not_6_out, or_1_out, or_2_out, or_3_out, or_4_out, t_ff_1_q, t_ff_1_qn, t_ff_2_q, t_ff_2_qn, t_ff_3_q,
       t_ff_3_qn, t_ff_4_q, t_ff_4_qn;

  Clock clock_1 (.out(clock_1_out));
  not not_1 (not_1_out, Decrescente);
  and and_1 (and_1_out, clock_1_out, Decrescente);
  and and_2 (and_2_out, clock_1_out, not_1_out);
  T_Flip_Flop #(.trigger("falling")) t_ff_1 (
    .clk(and_2_out), .T(1'b1), .Q(t_ff_1_q), .Qn(t_ff_1_qn), .reset(and_7_out));  // open: preset, en
  not not_2 (not_2_out, and_1_out);
  and and_3 (and_3_out, t_ff_1_q, not_2_out);
  Conversor_D_1 conversor_d_1_1 (
    .A(or_4_out), .B(or_3_out), .C(or_2_out), .D(or_1_out), .a_2(conversor_d_1_1_a_2),
    .b_2(conversor_d_1_1_b_2), .c_2(conversor_d_1_1_c_2), .d_2(conversor_d_1_1_d_2), .e(conversor_d_1_1_e),
    .f(conversor_d_1_1_f), .g(conversor_d_1_1_g));
  and and_4 (and_4_out, t_ff_1_qn, and_1_out);
  or or_1 (or_1_out, and_3_out, and_4_out);
  _7_Segment_Display u_7_segment_display_1 (
    .g(conversor_d_1_1_g), .f(conversor_d_1_1_f), .a(conversor_d_1_1_a_2), .b(conversor_d_1_1_b_2),
    .e(conversor_d_1_1_e), .d(conversor_d_1_1_d_2), .c(conversor_d_1_1_c_2));  // open: dp
  T_Flip_Flop #(.trigger("falling")) t_ff_2 (
    .clk(or_1_out), .T(1'b1), .Q(t_ff_2_q), .Qn(t_ff_2_qn), .reset(and_7_out));  // open: preset, en
  not not_3 (not_3_out, and_1_out);
  and and_5 (and_5_out, t_ff_2_q, not_3_out);
  _7_Segment_Display u_7_segment_display_2 (
    .g(conversor_d_15_1_g), .f(conversor_d_15_1_f), .a(conversor_d_15_1_a_2), .b(conversor_d_15_1_b_2),
    .e(conversor_d_15_1_e), .d(conversor_d_15_1_d_2), .c(conversor_d_15_1_c_2));  // open: dp
  Conversor_D_15 conversor_d_15_1 (
    .A(or_4_out), .B(or_3_out), .C(or_2_out), .D(or_1_out), .a_2(conversor_d_15_1_a_2),
    .b_2(conversor_d_15_1_b_2), .c_2(conversor_d_15_1_c_2), .d_2(conversor_d_15_1_d_2),
    .e(conversor_d_15_1_e), .f(conversor_d_15_1_f), .g(conversor_d_15_1_g));
  and and_6 (and_6_out, t_ff_2_qn, and_1_out);
  or or_2 (or_2_out, and_5_out, and_6_out);
  and and_7 (and_7_out, or_4_out, or_3_out, not_4_out, or_1_out);
  T_Flip_Flop #(.trigger("falling")) t_ff_3 (
    .clk(or_2_out), .T(1'b1), .Q(t_ff_3_q), .Qn(t_ff_3_qn), .reset(and_7_out));  // open: preset, en
  not not_4 (not_4_out, or_2_out);
  not not_5 (not_5_out, and_1_out);
  and and_8 (and_8_out, t_ff_3_q, not_5_out);
  and and_9 (and_9_out, t_ff_3_qn, and_1_out);
  or or_3 (or_3_out, and_8_out, and_9_out);
  T_Flip_Flop #(.trigger("falling")) t_ff_4 (
    .clk(or_3_out), .T(1'b1), .Q(t_ff_4_q), .Qn(t_ff_4_qn), .reset(and_7_out));  // open: preset, en
  not not_6 (not_6_out, and_1_out);
  and and_10 (and_10_out, t_ff_4_q, not_6_out);
  or or_4 (or_4_out, and_10_out, and_11_out);
  and and_11 (and_11_out, t_ff_4_qn, and_1_out);
endmodule

module Prova (
  input  Decrescente,
  input  in_2,
  input  in_3,
  input  in_4,
  input  in_5,
  input  in_6,
  output out_7,
  output out_8,
  output out_9,
  output out_10,
  output out_11
);

  wire and_1_out, and_2_out, and_3_out, and_4_out, and_5_out, and_6_out, and_7_out, and_8_out, and_9_out,
       and_10_out, and_11_out, and_12_out, clock_1_out, conversor_d_1_1_a_2, conversor_d_1_1_b_2,
       conversor_d_1_1_c_2, conversor_d_1_1_d_2, conversor_d_1_1_e, conversor_d_1_1_f, conversor_d_1_1_g,
       conversor_d_15_1_a_2, conversor_d_15_1_b_2, conversor_d_15_1_c_2, conversor_d_15_1_d_2,
       conversor_d_15_1_e, conversor_d_15_1_f, conversor_d_15_1_g, flip_flop_t_2_0_1_q,
       flip_flop_t_2_0_1_q_prime, flip_flop_t_2_0_2_q, flip_flop_t_2_0_2_q_prime, flip_flop_t_2_0_3_q,
       flip_flop_t_2_0_3_q_prime, flip_flop_t_2_0_4_q, flip_flop_t_2_0_4_q_prime, flip_flop_t_2_0_5_q,
       flip_flop_t_2_0_5_q_prime, not_1_out, not_2_out, not_3_out, not_4_out, not_5_out, not_6_out;

  teste teste_1 ();  // open: in_1, in_2, in_3, in_4, in_5, in_6, in_7, in_8, out_9, out_10, out_11, out_12, out_13, out_14, out_15, out_16, out_17, out_18
  Clock clock_1 (.out(clock_1_out));
  not not_1 (not_1_out, Decrescente);
  and and_1 (and_1_out, clock_1_out, Decrescente);
  and and_2 (and_2_out, clock_1_out, not_1_out);
  Flip_Flop_T_2_0 flip_flop_t_2_0_1 (
    .Clock(and_2_out), .T(1'b1), .Reset(in_2), .Q(flip_flop_t_2_0_1_q), .Q_prime(flip_flop_t_2_0_1_q_prime));
  not not_2 (not_2_out, and_1_out);
  and and_3 (and_3_out, flip_flop_t_2_0_1_q, not_2_out);
  Conversor_D_1 conversor_d_1_1 (
    .A(out_8), .B(out_9), .C(out_10), .D(out_11), .a_2(conversor_d_1_1_a_2), .b_2(conversor_d_1_1_b_2),
    .c_2(conversor_d_1_1_c_2), .d_2(conversor_d_1_1_d_2), .e(conversor_d_1_1_e), .f(conversor_d_1_1_f),
    .g(conversor_d_1_1_g));
  and and_4 (and_4_out, flip_flop_t_2_0_1_q_prime, and_1_out);
  or or_1 (out_11, and_3_out, and_4_out);
  _7_Segment_Display u_7_segment_display_1 (
    .g(conversor_d_1_1_g), .f(conversor_d_1_1_f), .a(conversor_d_1_1_a_2), .b(conversor_d_1_1_b_2),
    .e(conversor_d_1_1_e), .d(conversor_d_1_1_d_2), .c(conversor_d_1_1_c_2));  // open: dp
  Flip_Flop_T_2_0 flip_flop_t_2_0_2 (
    .Clock(out_11), .T(1'b1), .Reset(in_3), .Q(flip_flop_t_2_0_2_q), .Q_prime(flip_flop_t_2_0_2_q_prime));
  not not_3 (not_3_out, and_1_out);
  and and_5 (and_5_out, flip_flop_t_2_0_2_q, not_3_out);
  _7_Segment_Display u_7_segment_display_2 (
    .g(conversor_d_15_1_g), .f(conversor_d_15_1_f), .a(conversor_d_15_1_a_2), .b(conversor_d_15_1_b_2),
    .e(conversor_d_15_1_e), .d(conversor_d_15_1_d_2), .c(conversor_d_15_1_c_2));  // open: dp
  Conversor_D_15 conversor_d_15_1 (
    .A(out_8), .B(out_9), .C(out_10), .D(out_11), .a_2(conversor_d_15_1_a_2), .b_2(conversor_d_15_1_b_2),
    .c_2(conversor_d_15_1_c_2), .d_2(conversor_d_15_1_d_2), .e(conversor_d_15_1_e), .f(conversor_d_15_1_f),
    .g(conversor_d_15_1_g));
  and and_6 (and_6_out, flip_flop_t_2_0_2_q_prime, and_1_out);
  or or_2 (out_10, and_5_out, and_6_out);
  Flip_Flop_T_2_0 flip_flop_t_2_0_3 (
    .Clock(out_10), .T(1'b1), .Reset(in_4), .Q(flip_flop_t_2_0_3_q), .Q_prime(flip_flop_t_2_0_3_q_prime));
  not not_4 (not_4_out, and_1_out);
  and and_7 (and_7_out, flip_flop_t_2_0_3_q, not_4_out);
  and and_8 (and_8_out, flip_flop_t_2_0_3_q_prime, and_1_out);
  or or_3 (out_9, and_7_out, and_8_out);
  Flip_Flop_T_2_0 flip_flop_t_2_0_4 (
    .Clock(out_9), .T(1'b1), .Reset(in_5), .Q(flip_flop_t_2_0_4_q), .Q_prime(flip_flop_t_2_0_4_q_prime));
  not not_5 (not_5_out, and_1_out);
  and and_9 (and_9_out, flip_flop_t_2_0_4_q, not_5_out);
  or or_4 (out_8, and_9_out, and_10_out);
  and and_10 (and_10_out, flip_flop_t_2_0_4_q_prime, and_1_out);
  Flip_Flop_T_2_0 flip_flop_t_2_0_5 (
    .Clock(out_8), .T(1'b1), .Reset(in_6), .Q(flip_flop_t_2_0_5_q), .Q_prime(flip_flop_t_2_0_5_q_prime));
  not not_6 (not_6_out, and_1_out);
  and and_11 (and_11_out, flip_flop_t_2_0_5_q, not_6_out);
  or or_5 (out_7, and_11_out, and_12_out);
  and and_12 (and_12_out, flip_flop_t_2_0_5_q_prime, and_1_out);
endmodule

module Alteracao (
  input  _0___Crescente__1___Decrescente
);

  wire and_1_out, and_2_out, and_3_out, and_4_out, and_5_out, and_6_out, and_7_out, and_8_out, and_9_out,
       and_10_out, and_11_out, clock_1_out, conversor_d_1_1_a_2, conversor_d_1_1_b_2, conversor_d_1_1_c_2,
       conversor_d_1_1_d_2, conversor_d_1_1_e, conversor_d_1_1_f, conversor_d_1_1_g, conversor_d_15_1_a_2,
       conversor_d_15_1_b_2, conversor_d_15_1_c_2, conversor_d_15_1_d_2, conversor_d_15_1_e,
       conversor_d_15_1_f, conversor_d_15_1_g, flip_flop_t_2_0_1_q, flip_flop_t_2_0_1_q_prime,
       flip_flop_t_2_0_2_q, flip_flop_t_2_0_2_q_prime, flip_flop_t_2_0_3_q, flip_flop_t_2_0_3_q_prime,
       flip_flop_t_2_0_4_q, flip_flop_t_2_0_4_q_prime, not_1_out, not_2_out, not_3_out, not_4_out, not_5_out,
       not_6_out, not_7_out, or_1_out, or_2_out, or_3_out, or_4_out;

  Clock clock_1 (.out(clock_1_out));
  not not_1 (not_1_out, _0___Crescente__1___Decrescente);
  and and_1 (and_1_out, clock_1_out, _0___Crescente__1___Decrescente);
  and and_2 (and_2_out, clock_1_out, not_1_out);
  Flip_Flop_T_2_0 flip_flop_t_2_0_1 (
    .Clock(and_2_out), .T(1'b1), .Reset(and_7_out), .Q(flip_flop_t_2_0_1_q),
    .Q_prime(flip_flop_t_2_0_1_q_prime));
  not not_2 (not_2_out, and_1_out);
  and and_3 (and_3_out, flip_flop_t_2_0_1_q, not_2_out);
  Conversor_D_1 conversor_d_1_1 (
    .A(or_4_out), .B(or_3_out), .C(or_2_out), .D(or_1_out), .a_2(conversor_d_1_1_a_2),
    .b_2(conversor_d_1_1_b_2), .c_2(conversor_d_1_1_c_2), .d_2(conversor_d_1_1_d_2), .e(conversor_d_1_1_e),
    .f(conversor_d_1_1_f), .g(conversor_d_1_1_g));
  and and_4 (and_4_out, flip_flop_t_2_0_1_q_prime, and_1_out);
  or or_1 (or_1_out, and_3_out, and_4_out);
  _7_Segment_Display u_7_segment_display_1 (
    .g(conversor_d_1_1_g), .f(conversor_d_1_1_f), .a(conversor_d_1_1_a_2), .b(conversor_d_1_1_b_2),
    .e(conversor_d_1_1_e), .d(conversor_d_1_1_d_2), .c(conversor_d_1_1_c_2));  // open: dp
  Flip_Flop_T_2_0 flip_flop_t_2_0_2 (
    .Clock(or_1_out), .T(1'b1), .Reset(and_7_out), .Q(flip_flop_t_2_0_2_q),
    .Q_prime(flip_flop_t_2_0_2_q_prime));
  not not_3 (not_3_out, and_1_out);
  and and_5 (and_5_out, flip_flop_t_2_0_2_q, not_3_out);
  _7_Segment_Display u_7_segment_display_2 (
    .g(conversor_d_15_1_g), .f(conversor_d_15_1_f), .a(conversor_d_15_1_a_2), .b(conversor_d_15_1_b_2),
    .e(conversor_d_15_1_e), .d(conversor_d_15_1_d_2), .c(conversor_d_15_1_c_2));  // open: dp
  Conversor_D_15 conversor_d_15_1 (
    .A(or_4_out), .B(or_3_out), .C(or_2_out), .D(or_1_out), .a_2(conversor_d_15_1_a_2),
    .b_2(conversor_d_15_1_b_2), .c_2(conversor_d_15_1_c_2), .d_2(conversor_d_15_1_d_2),
    .e(conversor_d_15_1_e), .f(conversor_d_15_1_f), .g(conversor_d_15_1_g));
  and and_6 (and_6_out, flip_flop_t_2_0_2_q_prime, and_1_out);
  or or_2 (or_2_out, and_5_out, and_6_out);
  and and_7 (and_7_out, or_4_out, or_3_out, not_4_out, not_5_out);
  Flip_Flop_T_2_0 flip_flop_t_2_0_3 (
    .Clock(or_2_out), .T(1'b1), .Reset(and_7_out), .Q(flip_flop_t_2_0_3_q),
    .Q_prime(flip_flop_t_2_0_3_q_prime));
  not not_4 (not_4_out, or_2_out);
  not not_5 (not_5_out, or_1_out);
  not not_6 (not_6_out, and_1_out);
  and and_8 (and_8_out, flip_flop_t_2_0_3_q, not_6_out);
  and and_9 (and_9_out, flip_flop_t_2_0_3_q_prime, and_1_out);
  or or_3 (or_3_out, and_8_out, and_9_out);
  Flip_Flop_T_2_0 flip_flop_t_2_0_4 (
    .Clock(or_3_out), .T(1'b1), .Reset(and_7_out), .Q(flip_flop_t_2_0_4_q),
    .Q_prime(flip_flop_t_2_0_4_q_prime));
  not not_7 (not_7_out, and_1_out);
  and and_10 (and_10_out, flip_flop_t_2_0_4_q, not_7_out);
  or or_4 (or_4_out, and_10_out, and_11_out);
  and and_11 (and_11_out, flip_flop_t_2_0_4_q_prime, and_1_out);
endmodule
