// Logisim project Contadores.circ as structural Verilog: 4 circuits, main circuit main
module main (
);

  wire clock_1_out, contador_5_1_q0, contador_5_1_q1, contador_5_1_q2, contador_9_1_q0, contador_9_1_q1,
       contador_9_1_q2, contador_9_1_q3, conversor_d_9_1_a_2, conversor_d_9_1_b_2, conversor_d_9_1_c_2,
       conversor_d_9_1_d_2, conversor_d_9_1_e, conversor_d_9_1_f, conversor_d_9_1_g, conversor_d_9_2_a_2,
       conversor_d_9_2_b_2, conversor_d_9_2_c_2, conversor_d_9_2_d_2, conversor_d_9_2_e, conversor_d_9_2_f,
       conversor_d_9_2_g;

  Clock clock_1 (.out(clock_1_out));
  _7_Segment_Display u_7_segment_display_1 (
    .g(conversor_d_9_1_g), .f(conversor_d_9_1_f), .a(conversor_d_9_1_a_2), .b(conversor_d_9_1_b_2),
    .e(conversor_d_9_1_e), .d(conversor_d_9_1_d_2), .c(conversor_d_9_1_c_2));  // open: dp
  Conversor_D_9 conversor_d_9_1 (
    .A(1'b0), .B(contador_5_1_q2), .C(contador_5_1_q1), .D(contador_5_1_q0), .a_2(conversor_d_9_1_a_2),
    .b_2(conversor_d_9_1_b_2), .c_2(conversor_d_9_1_c_2), .d_2(conversor_d_9_1_d_2), .e(conversor_d_9_1_e),
    .f(conversor_d_9_1_f), .g(conversor_d_9_1_g));
  Contador_5 contador_5_1 (.Clock(contador_9_1_q3), .Q0(contador_5_1_q0), .Q1(contador_5_1_q1), .Q2(contador_5_1_q2));
  Conversor_D_9 conversor_d_9_2 (
    .A(contador_9_1_q3), .B(contador_9_1_q2), .C(contador_9_1_q1), .D(contador_9_1_q0),
    .a_2(conversor_d_9_2_a_2), .b_2(conversor_d_9_2_b_2), .c_2(conversor_d_9_2_c_2),
    .d_2(conversor_d_9_2_d_2), .e(conversor_d_9_2_e), .f(conversor_d_9_2_f), .g(conversor_d_9_2_g));
  _7_Segment_Display u_7_segment_display_2 (
    .g(conversor_d_9_2_g), .f(conversor_d_9_2_f), .a(conversor_d_9_2_a_2), .b(conversor_d_9_2_b_2),
    .e(conversor_d_9_2_e), .d(conversor_d_9_2_d_2), .c(conversor_d_9_2_c_2));  // open: dp
  Contador_9 contador_9_1 (
    .Clock(clock_1_out), .Q0(contador_9_1_q0), .Q1(contador_9_1_q1), .Q2(contador_9_1_q2),
    .Q3(contador_9_1_q3));
endmodule

module Contador_5 (
  input  Clock,
  output Q0,
  output Q1,
  output Q2
);

  wire and_1_out, not_1_out;

  T_Flip_Flop #(.trigger("falling")) t_ff_1 (.clk(Clock), .T(1'b1), .Q(Q0), .reset(and_1_out));  // open: Qn, preset, en
  T_Flip_Flop #(.trigger("falling")) t_ff_2 (.clk(Q0), .T(1'b1), .Q(Q1), .reset(and_1_out));  // open: Qn, preset, en
  not not_1 (not_1_out, Q0);
  and and_1 (and_1_out, not_1_out, Q1, Q2);
  T_Flip_Flop #(.trigger("falling")) t_ff_3 (.clk(Q1), .T(1'b1), .Q(Q2), .reset(and_1_out));  // open: Qn, preset, en
endmodule

module Contador_9 (
  input  Clock,
  output Q0,
  output Q1,
  output Q2,
  output Q3
);

  wire and_1_out, not_1_out, not_2_out;

  T_Flip_Flop #(.trigger("falling")) t_ff_1 (.clk(Clock), .T(1'b1), .Q(Q0), .reset(and_1_out));  // open: Qn, preset, en
  T_Flip_Flop #(.trigger("falling")) t_ff_2 (.clk(Q0), .T(1'b1), .Q(Q1), .reset(and_1_out));  // open: Qn, preset, en
  not not_1 (not_1_out, Q0);
  and and_1 (and_1_out, not_1_out, Q1, not_2_out, Q3);
  T_Flip_Flop #(.trigger("falling")) t_ff_3 (.clk(Q1), .T(1'b1), .Q(Q2), .reset(and_1_out));  // open: Qn, preset, en
  not not_2 (not_2_out, Q2);
  T_Flip_Flop #(.trigger("falling")) t_ff_4 (.clk(Q2), .T(1'b1), .Q(Q3), .reset(and_1_out));  // open: Qn, preset, en
endmodule

module Conversor_D_9 (
  input  A,
  input  B,
  input  C,
  input  D,
  output a_2,
  output b_2,
  output c_2,
  output d_2,
  output e,
  output f,
  output g
);

  wire and_1_out, and_2_out, and_3_out, and_4_out, and_5_out, and_6_out, and_7_out, and_8_out, and_9_out,
       and_10_out, and_11_out, and_12_out, and_13_out, and_14_out, and_15_out, and_16_out, not_1_out,
       not_2_out, not_3_out, not_4_out, not_5_out, not_6_out, not_7_out, not_8_out, not_9_out, not_10_out,
       not_11_out, not_12_out, not_13_out, not_14_out, not_15_out, not_16_out, not_17_out, not_18_out,
       not_19_out, not_20_out, not_21_out;

  not not_1 (not_1_out, B);
  and and_1 (and_1_out, not_1_out, not_2_out);
  not not_2 (not_2_out, D);
  and and_2 (and_2_out, B, D);
  not not_3 (not_3_out, B);
  not not_4 (not_4_out, C);
  and and_3 (and_3_out, not_4_out, not_5_out);
  not not_5 (not_5_out, D);
  and and_4 (and_4_out, C, D);
  not not_6 (not_6_out, C);
  or or_1 (c_2, not_6_out, D, B);
  not not_7 (not_7_out, B);
  and and_5 (and_5_out, not_7_out, not_8_out);
  not not_8 (not_8_out, D);
  not not_9 (not_9_out, B);
  and and_6 (and_6_out, not_9_out, C);
  and and_7 (and_7_out, C, not_10_out);
  not not_10 (not_10_out, D);
  not not_11 (not_11_out, C);
  and and_8 (and_8_out, B, not_11_out, D);
  not not_12 (not_12_out, B);
  and and_9 (and_9_out, not_12_out, not_13_out);
  not not_13 (not_13_out, D);
  and and_10 (and_10_out, C, not_14_out);
  not not_14 (not_14_out, D);
  not not_15 (not_15_out, C);
  and and_11 (and_11_out, not_15_out, not_16_out);
  not not_16 (not_16_out, D);
  and and_12 (and_12_out, B, not_17_out);
  not not_17 (not_17_out, C);
  and and_13 (and_13_out, B, not_18_out);
  not not_18 (not_18_out, D);
  not not_19 (not_19_out, B);
  and and_14 (and_14_out, not_19_out, C);
  and and_15 (and_15_out, B, not_20_out);
  not not_20 (not_20_out, C);
  and and_16 (and_16_out, B, not_21_out);
  not not_21 (not_21_out, D);
  or or_2 (a_2, and_1_out, C, and_2_out, A);
  or or_3 (b_2, not_3_out, and_3_out, and_4_out);
  or or_4 (d_2, and_5_out, and_6_out, and_7_out, and_8_out, A);
  or or_5 (e, and_9_out, and_10_out);
  or or_6 (f, and_11_out, and_12_out, and_13_out, A);
  or or_7 (g, and_14_out, and_15_out, and_16_out, A);
endmodule
