// Logisim project Ex2.circ as structural Verilog: 4 circuits, main circuit main
module main (
  input  _0___Crescente___1___Decrescente
);

  wire and_1_out, and_2_out, and_3_out, and_4_out, and_5_out, and_6_out, and_7_out, and_8_out, and_9_out,
       and_10_out, clock_1_out, conversor_d_1_1_a_2, conversor_d_1_1_b_2, conversor_d_1_1_c_2,
       conversor_d_1_1_d_2, conversor_d_1_1_e, conversor_d_1_1_f, conversor_d_1_1_g, conversor_d_15_1_a_2,
       conversor_d_15_1_b_2, conversor_d_15_1_c_2, conversor_d_15_1_d_2, conversor_d_15_1_e,
       conversor_d_15_1_f, conversor_d_15_1_g, not_1_out, not_2_out, not_3_out, not_4_out, not_5_out,
       or_1_out, or_2_out, or_3_out, or_4_out, t_ff_1_q, t_ff_1_qn, t_ff_2_q, t_ff_2_qn, t_ff_3_q, t_ff_3_qn,
       t_ff_4_q, t_ff_4_qn;

  Clock clock_1 (.out(clock_1_out));
  not not_1 (not_1_out, _0___Crescente___1___Decrescente);
  and and_1 (and_1_out, clock_1_out, _0___Crescente___1___Decrescente);
  and and_2 (and_2_out, clock_1_out, not_1_out);
  T_Flip_Flop #(.trigger("falling")) t_ff_1 (
    .clk(and_2_out), .T(1'b1), .Q(t_ff_1_q), .Qn(t_ff_1_qn));  // open: preset, reset, en
  not not_2 (not_2_out, and_1_out);
  and and_3 (and_3_out, t_ff_1_q, not_2_out);
  Conversor_D_1 conversor_d_1_1 (
    .A(or_4_out), .B(or_3_out), .C(or_2_out), .D(or_1_out), .a_2(conversor_d_1_1_a_2),
    .b_2(conversor_d_1_1_b_2), .c_2(conversor_d_1_1_c_2), .d_2(conversor_d_1_1_d_2), .e(conversor_d_1_1_e),
    .f(conversor_d_1_1_f), .g(conversor_d_1_1_g));
  and and_4 (and_4_out, t_ff_1_qn, and_1_out);
  or or_1 (or_1_out, and_3_out, and_4_out);
  _7_Segment_Display u_7_segment_display_1 (
    .g(conversor_d_1_1_g), .f(conversor_d_1_1_f), .a(conversor_d_1_1_a_2), .b(conversor_d_1_1_b_2),
    .e(conversor_d_1_1_e), .d(conversor_d_1_1_d_2), .c(conversor_d_1_1_c_2));  // open: dp
  T_Flip_Flop #(.trigger("falling")) t_ff_2 (
    .clk(or_1_out), .T(1'b1), .Q(t_ff_2_q), .Qn(t_ff_2_qn));  // open: preset, reset, en
  not not_3 (not_3_out, and_1_out);
  and and_5 (and_5_out, t_ff_2_q, not_3_out);
  _7_Segment_Display u_7_segment_display_2 (
    .g(conversor_d_15_1_g), .f(conversor_d_15_1_f), .a(conversor_d_15_1_a_2), .b(conversor_d_15_1_b_2),
    .e(conversor_d_15_1_e), .d(conversor_d_15_1_d_2), .c(conversor_d_15_1_c_2));  // open: dp
  Conversor_D_15 conversor_d_15_1 (
    .A(or_4_out), .B(or_3_out), .C(or_2_out), .D(or_1_out), .a_2(conversor_d_15_1_a_2),
    .b_2(conversor_d_15_1_b_2), .c_2(conversor_d_15_1_c_2), .d_2(conversor_d_15_1_d_2),
    .e(conversor_d_15_1_e), .f(conversor_d_15_1_f), .g(conversor_d_15_1_g));
  and and_6 (and_6_out, t_ff_2_qn, and_1_out);
  or or_2 (or_2_out, and_5_out, and_6_out);
  T_Flip_Flop #(.trigger("falling")) t_ff_3 (
    .clk(or_2_out), .T(1'b1), .Q(t_ff_3_q), .Qn(t_ff_3_qn));  // open: preset, reset, en
  not not_4 (not_4_out, and_1_out);
  and and_7 (and_7_out, t_ff_3_qn, and_1_out);
  and and_8 (and_8_out, t_ff_3_q, not_4_out);
  or or_3 (or_3_out, and_8_out, and_7_out);
  T_Flip_Flop #(.trigger("falling")) t_ff_4 (
    .clk(or_3_out), .T(1'b1), .Q(t_ff_4_q), .Qn(t_ff_4_qn));  // open: preset, reset, en
  not not_5 (not_5_out, and_1_out);
  and and_9 (and_9_out, t_ff_4_q, not_5_out);
  or or_4 (or_4_out, and_9_out, and_10_out);
  and and_10 (and_10_out, t_ff_4_qn, and_1_out);
endmodule

module Conversor_D_1 (
  input  A,
  input  B,
  input  C,
  input  D,
  output a_2,
  output b_2,
  output c_2,
  output d_2,
  output e,
  output f,
  output g
);

  wire and_1_out, and_2_out, and_3_out, and_4_out, not_1_out, not_2_out, not_3_out, not_4_out, not_5_out,
       not_6_out, not_7_out, not_8_out, not_9_out, not_10_out, not_11_out, not_12_out;

  not not_1 (not_1_out, A);
  not not_2 (not_2_out, B);
  and and_1 (and_1_out, not_2_out, not_3_out);
  not not_3 (not_3_out, C);
  not not_4 (not_4_out, A);
  not not_5 (not_5_out, B);
  and and_2 (and_2_out, not_5_out, not_6_out);
  not not_6 (not_6_out, C);
  not not_7 (not_7_out, A);
  not not_8 (not_8_out, B);
  and and_3 (and_3_out, not_8_out, not_9_out);
  not not_9 (not_9_out, C);
  not not_10 (not_10_out, A);
  not not_11 (not_11_out, B);
  and and_4 (and_4_out, not_11_out, not_12_out);
  not not_12 (not_12_out, C);
  or or_1 (a_2, not_1_out, and_1_out);
  or or_2 (d_2, not_4_out, and_2_out);
  or or_3 (e, not_7_out, and_3_out);
  or or_4 (f, not_10_out, and_4_out);

  assign b_2 = 1'b1;
  assign c_2 = 1'b1;
  assign g = 1'b0;
endmodule

module Conversor_D_15 (
  input  A,
  input  B,
  input  C,
  input  D,
  output a_2,
  output b_2,
  output c_2,
  output d_2,
  output e,
  output f,
  output g
);

  wire and_1_out, and_2_out, and_3_out, and_4_out, and_5_out, and_6_out, and_7_out, and_8_out, and_9_out,
       and_10_out, and_11_out, and_12_out, and_13_out, and_14_out, and_15_out, and_16_out, and_17_out,
       and_18_out, and_19_out, and_20_out, and_21_out, and_22_out, and_23_out, and_24_out, and_25_out,
       and_26_out, and_27_out, and_28_out, and_29_out, and_30_out, and_31_out, not_1_out, not_2_out,
       not_3_out, not_4_out, not_5_out, not_6_out, not_7_out, not_8_out, not_9_out, not_10_out, not_11_out,
       not_12_out, not_13_out, not_14_out, not_15_out, not_16_out, not_17_out, not_18_out, not_19_out,
       not_20_out, not_21_out, not_22_out, not_23_out, not_24_out, not_25_out, not_26_out, not_27_out,
       not_28_out, not_29_out, not_30_out, not_31_out, not_32_out, not_33_out, not_34_out, not_35_out,
       not_36_out, not_37_out, not_38_out, not_39_out, not_40_out, not_41_out, not_42_out, not_43_out;

  not not_1 (not_1_out, B);
  and and_1 (and_1_out, not_1_out, not_2_out);
  not not_2 (not_2_out, D);
  not not_3 (not_3_out, A);
  and and_2 (and_2_out, not_3_out, C);
  and and_3 (and_3_out, B, D);
  and and_4 (and_4_out, A, not_4_out);
  not not_4 (not_4_out, C);
  not not_5 (not_5_out, B);
  not not_6 (not_6_out, C);
  and and_5 (and_5_out, not_6_out, not_7_out);
  not not_7 (not_7_out, D);
  not not_8 (not_8_out, A);
  and and_6 (and_6_out, not_8_out, C, D);
  and and_7 (and_7_out, A, not_9_out);
  not not_9 (not_9_out, C);
  and and_8 (and_8_out, A, not_10_out);
  not not_10 (not_10_out, D);
  not not_11 (not_11_out, A);
  and and_9 (and_9_out, not_11_out, not_12_out);
  not not_12 (not_12_out, C);
  and and_10 (and_10_out, B, C);
  and and_11 (and_11_out, A, not_13_out);
  not not_13 (not_13_out, B);
  not not_14 (not_14_out, B);
  and and_12 (and_12_out, not_14_out, not_15_out);
  not not_15 (not_15_out, D);
  not not_16 (not_16_out, A);
  and and_13 (and_13_out, not_16_out, not_17_out, C);
  not not_17 (not_17_out, B);
  not not_18 (not_18_out, A);
  and and_14 (and_14_out, not_18_out, C, not_19_out);
  not not_19 (not_19_out, D);
  and and_15 (and_15_out, B, not_20_out, D);
  not not_20 (not_20_out, C);
  and and_16 (and_16_out, A, not_21_out);
  not not_21 (not_21_out, C);
  and and_17 (and_17_out, A, B, D);
  not not_22 (not_22_out, B);
  and and_18 (and_18_out, not_22_out, not_23_out);
  not not_23 (not_23_out, D);
  not not_24 (not_24_out, A);
  and and_19 (and_19_out, not_24_out, C, not_25_out);
  not not_25 (not_25_out, D);
  not not_26 (not_26_out, C);
  and and_20 (and_20_out, A, not_26_out, not_27_out);
  not not_27 (not_27_out, D);
  not not_28 (not_28_out, A);
  and and_21 (and_21_out, not_28_out, not_29_out, not_30_out);
  not not_29 (not_29_out, C);
  not not_30 (not_30_out, D);
  not not_31 (not_31_out, A);
  and and_22 (and_22_out, not_31_out, B, not_32_out);
  not not_32 (not_32_out, C);
  not not_33 (not_33_out, A);
  and and_23 (and_23_out, not_33_out, B, not_34_out);
  not not_34 (not_34_out, D);
  and and_24 (and_24_out, A, not_35_out, not_36_out);
  not not_35 (not_35_out, B);
  not not_36 (not_36_out, C);
  and and_25 (and_25_out, A, not_37_out, not_38_out);
  not not_37 (not_37_out, B);
  not not_38 (not_38_out, D);
  and and_26 (and_26_out, A, B, C);
  not not_39 (not_39_out, A);
  not not_40 (not_40_out, B);
  and and_27 (and_27_out, not_39_out, not_40_out, C);
  and and_28 (and_28_out, B, not_41_out);
  not not_41 (not_41_out, C);
  and and_29 (and_29_out, B, not_42_out);
  not not_42 (not_42_out, D);
  and and_30 (and_30_out, A, not_43_out);
  not not_43 (not_43_out, C);
  and and_31 (and_31_out, A, B);
  or or_1 (a_2, and_1_out, and_2_out, and_3_out, and_4_out);
  or or_2 (b_2, not_5_out, and_5_out, and_6_out, and_7_out, and_8_out);
  or or_3 (c_2, and_9_out, D, and_10_out, and_11_out);
  or or_4 (e, and_18_out, and_19_out, and_20_out);
  or or_5 (g, and_27_out, and_28_out, and_29_out, and_30_out, and_31_out);
  or or_6 (d_2, and_12_out, and_13_out, and_14_out, and_15_out, and_16_out, and_17_out);
  or or_7 (f, and_21_out, and_22_out, and_23_out, and_24_out, and_25_out, and_26_out);
endmodule

module Flip_Flop_2_0 (
  input  Clock,
  input  T,
  input  Reset,
  output Q,
  output Q_prime
);

  wire nand_1_out, nand_2_out, nand_3_out, nand_4_out, nand_5_out, nand_6_out, not_1_out, not_2_out;

  not not_1 (not_1_out, Clock);
  nand nand_1 (nand_1_out, Q_prime, T, Clock);
  nand nand_2 (nand_2_out, Clock, T, Q);
  not not_2 (not_2_out, Reset);
  nand nand_3 (nand_3_out, nand_1_out, nand_4_out);
  nand nand_4 (nand_4_out, nand_3_out, nand_2_out, not_2_out);
  nand nand_5 (nand_5_out, nand_3_out, not_1_out);
  nand nand_6 (nand_6_out, nand_4_out, not_1_out);
  nand nand_7 (Q, not_2_out, nand_5_out, Q_prime);
  nand nand_8 (Q_prime, Q, nand_6_out, not_2_out);

  // Notes on the sheet:
  //   Utilizado no trabalho mas nesta questao preferi usar o Flip flop T do prorio Logisim
endmodule
