// Logisim project Flip Flop JK.circ as structural Verilog: 3 circuits, main circuit main
module main (
  input  T,
  input  Clock,
  input  Reset,
  output Q,
  output Q_prime
);

  wire nand_1_out, nand_2_out, nand_3_out, nand_4_out, nand_5_out, nand_6_out, not_1_out, not_2_out;

  nand nand_1 (nand_1_out, Q_prime, T, Clock);
  nand nand_2 (nand_2_out, Clock, T, Q);
  not not_1 (not_1_out, Clock);
  not not_2 (not_2_out, Reset);
  nand nand_3 (nand_3_out, nand_1_out, nand_4_out);
  nand nand_4 (nand_4_out, nand_3_out, nand_2_out, not_2_out);
  nand nand_5 (nand_5_out, nand_3_out, not_1_out);
  nand nand_6 (nand_6_out, nand_4_out, not_1_out);
  nand nand_7 (Q, not_2_out, nand_5_out, Q_prime);
  nand nand_8 (Q_prime, Q, nand_6_out, not_2_out);
endmodule

module Padrao (
  input  in_1,
  input  in_2,
  input  in_3,
  input  in_4,
  output out_5,
  output out_6,
  output out_7,
  output out_8
);

  wire clock_1_out, clock_2_out, nand_1_out, nand_2_out, nand_3_out, nand_4_out, nand_5_out, nand_6_out,
       nand_7_out, nand_8_out, nand_9_out, nand_10_out, nand_11_out, nand_12_out, not_1_out, not_2_out,
       not_3_out;

  Clock clock_1 (.out(clock_1_out));
  Clock clock_2 (.out(clock_2_out));
  not not_1 (not_1_out, clock_2_out);
  not not_2 (not_2_out, clock_1_out);
  not not_3 (not_3_out, not_1_out);
  nand nand_1 (nand_1_out, out_6, in_1, clock_1_out);
  nand nand_2 (nand_2_out, clock_1_out, in_2, out_5);
  nand nand_3 (nand_3_out, out_8, in_3, not_1_out);
  nand nand_4 (nand_4_out, not_1_out, in_4, out_7);
  nand nand_5 (nand_5_out, nand_1_out, nand_6_out);
  nand nand_6 (nand_6_out, nand_5_out, nand_2_out);
  nand nand_7 (nand_7_out, nand_3_out, nand_8_out);
  nand nand_8 (nand_8_out, nand_7_out, nand_4_out);
  nand nand_9 (nand_9_out, nand_5_out, not_2_out);
  nand nand_10 (nand_10_out, not_2_out, nand_6_out);
  nand nand_11 (nand_11_out, nand_7_out, not_3_out);
  nand nand_12 (nand_12_out, not_3_out, nand_8_out);
  nand nand_13 (out_5, nand_9_out, out_6);
  nand nand_14 (out_6, out_5, nand_10_out);
  nand nand_15 (out_7, nand_11_out, out_8);
  nand nand_16 (out_8, out_7, nand_12_out);
endmodule

module Flip_Flop_T (
  input  in_1,
  input  in_2,
  output out_3,
  output out_4
);

  wire clock_1_out, nand_1_out, nand_2_out, nand_3_out, nand_4_out, nand_5_out, nand_6_out, not_1_out,
       not_2_out;

  Clock clock_1 (.out(clock_1_out));
  nand nand_1 (nand_1_out, out_4, in_1, clock_1_out);
  nand nand_2 (nand_2_out, clock_1_out, in_1, out_3);
  not not_1 (not_1_out, clock_1_out);
  not not_2 (not_2_out, in_2);
  nand nand_3 (nand_3_out, nand_1_out, nand_4_out);
  nand nand_4 (nand_4_out, nand_3_out, nand_2_out, not_2_out);
  nand nand_5 (nand_5_out, nand_3_out, not_1_out);
  nand nand_6 (nand_6_out, nand_4_out, not_1_out);
  nand nand_7 (out_3, not_2_out, nand_5_out, out_4);
  nand nand_8 (out_4, out_3, nand_6_out, not_2_out);
endmodule
