// Logisim project Roteiro 2.circ as structural Verilog: 6 circuits, main circuit main
module main (
  input  A,
  input  B,
  input  C,
  output S
);

  wire and_1_out, and_2_out, and_3_out, not_1_out, not_2_out;

  not not_1 (not_1_out, A);
  not not_2 (not_2_out, B);
  and and_1 (and_1_out, not_1_out, C);
  and and_2 (and_2_out, A, not_2_out, C);
  and and_3 (and_3_out, C, B, A);
  or or_1 (S, and_1_out, and_2_out, and_3_out);
endmodule

module Simplificada (
  input  A,
  input  B,
  input  C,
  output S
);


  assign S = C;
endmodule

module main2 (
  input  A,
  input  B,
  input  C,
  output S
);

  wire and_1_out, and_2_out, and_3_out, not_1_out, not_2_out;

  not not_1 (not_1_out, C);
  not not_2 (not_2_out, B);
  and and_1 (and_1_out, A, B, C);
  and and_2 (and_2_out, not_1_out, A);
  and and_3 (and_3_out, A, not_2_out);
  or or_1 (S, and_1_out, and_2_out, and_3_out);
endmodule

module Simplificada2 (
  input  A,
  input  B,
  input  C,
  output S
);


  assign S = A;
endmodule

module main3 (
  input  A,
  input  B,
  input  C,
  input  D,
  output S
);

  wire and_1_out, and_2_out, and_3_out, and_4_out, and_5_out, not_1_out, not_2_out, not_3_out, not_4_out;

  not not_1 (not_1_out, C);
  not not_2 (not_2_out, A);
  not not_3 (not_3_out, B);
  not not_4 (not_4_out, D);
  and and_1 (and_1_out, A, not_3_out, not_4_out);
  and and_2 (and_2_out, not_4_out, not_1_out, not_3_out);
  and and_3 (and_3_out, not_3_out, not_1_out);
  and and_4 (and_4_out, C, D, not_2_out);
  and and_5 (and_5_out, D, B);
  or or_1 (S, and_1_out, and_2_out, and_3_out, and_4_out, and_5_out);
endmodule

module Simplifica3 (
  input  A,
  input  B,
  input  C,
  input  D,
  output S
);

  wire and_1_out, and_2_out, and_3_out, and_4_out, not_1_out, not_2_out, not_3_out, not_4_out, not_5_out;

  not not_1 (not_1_out, B);
  and and_1 (and_1_out, not_1_out, not_2_out);
  not not_2 (not_2_out, C);
  not not_3 (not_3_out, A);
  and and_2 (and_2_out, not_3_out, D);
  and and_3 (and_3_out, B, D);
  not not_4 (not_4_out, B);
  and and_4 (and_4_out, A, not_4_out, not_5_out);
  not not_5 (not_5_out, D);
  or or_1 (S, and_1_out, and_2_out, and_3_out, and_4_out);
endmodule
