// Logisim project Roteiro 3.circ as structural Verilog: 1 circuit, main circuit main
module main (
  input  A,
  input  B,
  output S
);

  wire nor_1_out, nor_2_out, nor_3_out, nor_4_out, nor_5_out;

  nor nor_1 (nor_1_out, B, B);
  nor nor_2 (nor_2_out, A, A);
  nor nor_3 (nor_3_out, A, nor_1_out);
  nor nor_4 (nor_4_out, nor_2_out, B);
  nor nor_5 (nor_5_out, nor_3_out, nor_4_out);
  nor nor_6 (S, nor_5_out, nor_5_out);
endmodule
