// Logisim project Somador1.circ as structural Verilog: 1 circuit, main circuit main
module main (
  input  a1,
  input  a0,
  input  C,
  input  b1,
  input  b0,
  output out_6,
  output s0,
  output C_2
);

  wire and_1_out, and_2_out, and_3_out, and_4_out, and_5_out, and_6_out, or_1_out;

  ExactlyOne xor_1 (.out(s0), .in0(a0), .in1(b0), .in2(C));
  and and_1 (and_1_out, a0, C);
  and and_2 (and_2_out, a0, b0);
  and and_3 (and_3_out, C, b0);
  or or_1 (or_1_out, and_1_out, and_2_out, and_3_out);
  ExactlyOne xor_2 (.out(out_6), .in0(a1), .in1(b1), .in2(or_1_out));
  and and_4 (and_4_out, a1, or_1_out);
  and and_5 (and_5_out, a1, b1);
  and and_6 (and_6_out, or_1_out, b1);
  or or_2 (C_2, and_4_out, and_5_out, and_6_out);
endmodule
