// Logisim project Teste1.circ as structural Verilog: 5 circuits, main circuit main
module main (
  input  A,
  input  B,
  input  C,
  input  D,
  output S
);

  wire and_1_out, and_2_out, not_1_out, not_2_out, or_1_out, or_2_out;

  and and_1 (and_1_out, B, C);
  and and_2 (and_2_out, A, B);
  not not_1 (not_1_out, and_2_out);
  or or_1 (or_1_out, A, and_1_out);
  or or_2 (or_2_out, D, not_1_out);
  not not_2 (not_2_out, or_1_out);
  and and_3 (S, not_2_out, or_2_out);
endmodule

module \nand  (
  input  A,
  input  B,
  input  C,
  input  D,
  output S
);

  wire nand_1_out, nand_2_out, nand_3_out, nand_4_out, nand_5_out;

  nand nand_1 (nand_1_out, A, A);
  nand nand_2 (nand_2_out, B, B);
  nand nand_3 (nand_3_out, C, C);
  nand nand_4 (nand_4_out, nand_1_out, nand_2_out);
  nand nand_5 (nand_5_out, nand_1_out, nand_3_out);
  nand nand_6 (S, nand_4_out, nand_5_out);
endmodule

module nand_verf (
  input  A,
  input  B,
  input  C,
  input  D,
  output S
);

  wire nand_1_out, nand_2_out, nand_3_out, nand_4_out, nand_5_out, nand_6_out, nand_7_out, nand_8_out,
       nand_9_out;

  nand nand_1 (nand_1_out, A, A);
  nand nand_2 (nand_2_out, B, C);
  nand nand_3 (nand_3_out, A, B);
  nand nand_4 (nand_4_out, nand_1_out, nand_2_out);
  nand nand_5 (nand_5_out, D, D);
  nand nand_6 (nand_6_out, nand_3_out, nand_3_out);
  nand nand_7 (nand_7_out, nand_4_out, nand_4_out);
  nand nand_8 (nand_8_out, nand_5_out, nand_6_out);
  nand nand_9 (nand_9_out, nand_7_out, nand_8_out);
  nand nand_10 (S, nand_9_out, nand_9_out);
endmodule

module main_simp (
  input  A,
  input  B,
  input  C,
  input  D,
  output S
);

  wire and_1_out, nand_1_out, nor_1_out, or_1_out;

  and and_1 (and_1_out, B, C);
  nand nand_1 (nand_1_out, A, B);
  nor nor_1 (nor_1_out, A, and_1_out);
  or or_1 (or_1_out, D, nand_1_out);
  and and_2 (S, nor_1_out, or_1_out);
endmodule

module \nor  (
  input  A,
  input  B,
  input  C,
  input  D,
  output S
);

  wire nor_1_out, nor_2_out, nor_3_out, nor_4_out, nor_5_out;

  nor nor_1 (nor_1_out, A, A);
  nor nor_2 (nor_2_out, B, B);
  nor nor_3 (nor_3_out, C, C);
  nor nor_4 (nor_4_out, nor_2_out, nor_3_out);
  nor nor_5 (nor_5_out, nor_1_out, nor_1_out);
  nor nor_6 (S, nor_5_out, nor_4_out);
endmodule
