// Logisim project display 7 segmentos.circ as structural Verilog: 3 circuits, main circuit main
module main (
  input  b,
  input  a,
  input  f,
  input  A_2,
  input  g,
  input  B_2,
  input  C,
  input  e,
  input  D,
  input  d_2,
  input  c_2,
  input  in_12
);

  wire conversor_1_a_2, conversor_1_b_2, conversor_1_c_2, conversor_1_d_2, conversor_1_e, conversor_1_f,
       conversor_1_g;

  _7_Segment_Display u_7_segment_display_1 (.g(g), .f(f), .a(a), .b(b), .e(e), .d(d_2), .c(c_2), .dp(in_12));
  Conversor conversor_1 (
    .A(A_2), .B(B_2), .C(C), .D(D), .a_2(conversor_1_a_2), .b_2(conversor_1_b_2), .c_2(conversor_1_c_2),
    .d_2(conversor_1_d_2), .e(conversor_1_e), .f(conversor_1_f), .g(conversor_1_g));
  _7_Segment_Display u_7_segment_display_2 (
    .g(conversor_1_g), .f(conversor_1_f), .a(conversor_1_a_2), .b(conversor_1_b_2), .e(conversor_1_e),
    .d(conversor_1_d_2), .c(conversor_1_c_2));  // open: dp
endmodule

module TESTE (
  input  A,
  input  B,
  input  C,
  input  D
);

  wire and_1_out, and_2_out, and_3_out, and_4_out, and_5_out, and_6_out, and_7_out, and_8_out, and_9_out,
       and_10_out, and_11_out, nand_1_out, nand_2_out, not_1_out, not_2_out, not_3_out, not_4_out, not_5_out,
       not_6_out, not_7_out, not_8_out, not_9_out, not_10_out, not_11_out, not_12_out, or_1_out, or_2_out,
       or_3_out, or_4_out, or_5_out, or_6_out;

  not not_1 (not_1_out, B);
  not not_2 (not_2_out, D);
  not not_3 (not_3_out, C);
  not not_4 (not_4_out, B);
  not not_5 (not_5_out, D);
  not not_6 (not_6_out, C);
  not not_7 (not_7_out, D);
  not not_8 (not_8_out, C);
  not not_9 (not_9_out, D);
  not not_10 (not_10_out, B);
  and and_1 (and_1_out, not_10_out, not_11_out);
  not not_11 (not_11_out, D);
  and and_2 (and_2_out, B, D);
  nand nand_1 (nand_1_out, C, D);
  and and_3 (and_3_out, C, D);
  not not_12 (not_12_out, C);
  or or_1 (or_1_out, not_12_out, B, D);
  nand nand_2 (nand_2_out, B, D);
  and and_4 (and_4_out, not_1_out, C);
  and and_5 (and_5_out, C, not_2_out);
  and and_6 (and_6_out, B, not_3_out, D);
  and and_7 (and_7_out, not_4_out, not_5_out);
  and and_8 (and_8_out, C, D);
  and and_9 (and_9_out, not_6_out, not_7_out);
  and and_10 (and_10_out, B, not_8_out);
  and and_11 (and_11_out, B, not_9_out);
  or or_2 (or_2_out, A, C, and_1_out, and_2_out);
  _7_Segment_Display u_7_segment_display_1 (
    .f(or_6_out), .a(or_2_out), .b(or_3_out), .e(or_5_out), .d(or_4_out), .c(or_1_out));  // open: g, dp
  or or_3 (or_3_out, B, nand_1_out, and_3_out);
  or or_4 (or_4_out, A, nand_2_out, and_4_out, and_5_out, and_6_out);
  or or_5 (or_5_out, and_7_out, and_8_out);
  or or_6 (or_6_out, A, and_9_out, and_10_out, and_11_out);
endmodule

module Conversor (
  input  A,
  input  B,
  input  C,
  input  D,
  output a_2,
  output b_2,
  output c_2,
  output d_2,
  output e,
  output f,
  output g
);

  wire and_1_out, and_2_out, and_3_out, and_4_out, and_5_out, and_6_out, and_7_out, and_8_out, and_9_out,
       and_10_out, and_11_out, and_12_out, and_13_out, and_14_out, and_15_out, and_16_out, not_1_out,
       not_2_out, not_3_out, not_4_out, not_5_out, not_6_out, not_7_out, not_8_out, not_9_out, not_10_out,
       not_11_out, not_12_out, not_13_out, not_14_out, not_15_out, not_16_out, not_17_out, not_18_out,
       not_19_out, not_20_out, not_21_out;

  not not_1 (not_1_out, B);
  and and_1 (and_1_out, not_1_out, not_2_out);
  not not_2 (not_2_out, D);
  and and_2 (and_2_out, B, D);
  not not_3 (not_3_out, B);
  not not_4 (not_4_out, C);
  and and_3 (and_3_out, not_4_out, not_5_out);
  not not_5 (not_5_out, D);
  and and_4 (and_4_out, C, D);
  not not_6 (not_6_out, C);
  or or_1 (c_2, not_6_out, D, B);
  not not_7 (not_7_out, B);
  and and_5 (and_5_out, not_7_out, not_8_out);
  not not_8 (not_8_out, D);
  not not_9 (not_9_out, B);
  and and_6 (and_6_out, not_9_out, C);
  and and_7 (and_7_out, C, not_10_out);
  not not_10 (not_10_out, D);
  not not_11 (not_11_out, C);
  and and_8 (and_8_out, B, not_11_out, D);
  not not_12 (not_12_out, B);
  and and_9 (and_9_out, not_12_out, not_13_out);
  not not_13 (not_13_out, D);
  and and_10 (and_10_out, C, not_14_out);
  not not_14 (not_14_out, D);
  not not_15 (not_15_out, C);
  and and_11 (and_11_out, not_15_out, not_16_out);
  not not_16 (not_16_out, D);
  and and_12 (and_12_out, B, not_17_out);
  not not_17 (not_17_out, C);
  and and_13 (and_13_out, B, not_18_out);
  not not_18 (not_18_out, D);
  not not_19 (not_19_out, B);
  and and_14 (and_14_out, not_19_out, C);
  and and_15 (and_15_out, B, not_20_out);
  not not_20 (not_20_out, C);
  and and_16 (and_16_out, B, not_21_out);
  not not_21 (not_21_out, D);
  or or_2 (a_2, and_1_out, C, and_2_out, A);
  or or_3 (b_2, not_3_out, and_3_out, and_4_out);
  or or_4 (d_2, and_5_out, and_6_out, and_7_out, and_8_out, A);
  or or_5 (e, and_9_out, and_10_out);
  or or_6 (f, and_11_out, and_12_out, and_13_out, A);
  or or_7 (g, and_14_out, and_15_out, and_16_out, A);
endmodule
